# Fritzing sketch fritzing file prototype (saved by Fritzing 0.9.10b)
breadboards: 1

parts:
  OLED_I2C1 = OLED 128x64 I2C Monochrome Display
  Part1 = Thumb Joystick
  M1 = ESP32-S2-DevKitC-1 [part_number=ESP32-S2-DevKitC-1]
  S1 = Pushbutton [package="[THT]"]
  S2 = Pushbutton [package="[THT]"]
  J1 = Piezo Speaker

nets:
  N1: OLED_I2C1.SDA, M1.pin_8
  N2: OLED_I2C1.SCK, M1.pin_9
  VDD: OLED_I2C1.VDD, Part1.VCC, M1.pin_1, M1.pin_2
  GND: OLED_I2C1.GND, Part1.GND, M1.pin_22, M1.pin_23, M1.pin_24, M1.pin_44, S1.Pin_3, S1.Pin_4, S2.Pin_3, S2.Pin_4, J1.pin1
  N3: Part1.HORZ, M1.pin_11
  N4: Part1.VERT, M1.pin_10
  N5: M1.pin_4, S1.Pin_1, S1.Pin_2
  N6: M1.pin_5, S2.Pin_1, S2.Pin_2
  N7: M1.pin_41, J1.pin2

custom parts:
  ESP32-S2-DevKitC-1: ESP32-S2-DevKitC-1 is an entry-level development board based on ESP32-S2-SOLO (on-board PCB antenna). It is based on the ESP32 microcontroller that boasts Wifi, Bluetooth, Ethernet and Low Power support all in a single chip. (vanepp) Feb 2022: converted to ESP32-S2-DevKitC-1. This module is 44pins long (2x22) and 11 pins width.
